// Logisim project processor.circ as structural Verilog: 1 circuit, main circuit main
module main (
);

  wire adder_1_cout, and_2_out, and_3_out, and_4_out, and_5_out, and_6_out, clock_1_out, comparator_1_eq,
       not_1_out, not_2_out, not_4_out, or_1_out, s_r_ff_1_q;
  wire [3:0] rom_1_data_2;
  wire [7:0] adder_1_out, and_1_out, counter_1_q, multiplexer_1_out, not_3_out, or_2_out, ram_1_data,
       register_1_q, rom_1_data, xor_1_out;

  Clock clock_1 (.out(clock_1_out));
  or or_1 (or_1_out, and_4_out, and_3_out, and_2_out);
  not not_1 (not_1_out, or_1_out);
  Counter counter_1 (
    .load(or_1_out), .D(rom_1_data), .count(not_1_out), .Q(counter_1_q), .clk(clock_1_out));  // open: carry, clr
  RAM ram_1 (.addr(rom_1_data), .data(ram_1_data), .clk(clock_1_out), .ld(not_2_out));  // open: sel, clr
  not not_2 (not_2_out, and_5_out);
  assign ram_1_data = and_5_out ? register_1_q : 8'bz;  // Controlled_Buffer controlled_buffer_1
  ROM #(.dataWidth(12)) rom_1 (.addr(counter_1_q), .data({rom_1_data, rom_1_data_2}));  // open: sel
  assign and_1_out = rom_1_data & register_1_q;  // AND_Gate and_1, 8 bits wide
  assign or_2_out = rom_1_data | register_1_q;  // OR_Gate or_2, 8 bits wide
  assign not_3_out = ~register_1_q;  // NOT_Gate not_3, 8 bits wide
  Adder adder_1 (.a(rom_1_data), .b(register_1_q), .out(adder_1_out), .cout(adder_1_cout));  // open: cin
  assign xor_1_out = rom_1_data ^ register_1_q;  // XOR_Gate xor_1, 8 bits wide
  and and_2 (and_2_out, rom_1_data_2[3], ~rom_1_data_2[2], ~rom_1_data_2[1], ~rom_1_data_2[0]);  // AND_Gate
  and and_3 (and_3_out, ~rom_1_data_2[2], ~rom_1_data_2[1], rom_1_data_2[0], comparator_1_eq, rom_1_data_2[3]);  // AND_Gate
  Multiplexer #(.select(4), .width(8), .enable("false")) multiplexer_1 (
    .in0(register_1_q), .in1(ram_1_data), .in2(rom_1_data), .in3(and_1_out), .in4(or_2_out), .in5(xor_1_out),
    .in6(not_3_out), .in7(register_1_q), .in8(register_1_q), .in9(register_1_q), .in10(register_1_q),
    .in11(adder_1_out), .in12(register_1_q), .in13(register_1_q), .in14(register_1_q), .in15(register_1_q),
    .out(multiplexer_1_out), .sel(rom_1_data_2));
  and and_4 (and_4_out, ~rom_1_data_2[0], ~rom_1_data_2[2], rom_1_data_2[1], rom_1_data_2[3], not_4_out);  // AND_Gate
  S_R_Flip_Flop s_r_ff_1 (.Q(s_r_ff_1_q), .preset(adder_1_cout), .reset(and_6_out));  // open: S, clk, R, Qn, en
  Register register_1 (.D(multiplexer_1_out), .Q(register_1_q), .clk(clock_1_out));  // open: en, clr
  not not_4 (not_4_out, s_r_ff_1_q);
  and and_5 (and_5_out, ~rom_1_data_2[3], rom_1_data_2[0], rom_1_data_2[1], rom_1_data_2[2]);  // AND_Gate
  Comparator comparator_1 (.a(register_1_q), .b({8{1'b0}}), .eq(comparator_1_eq));  // open: gt, lt
  and and_6 (and_6_out, ~rom_1_data_2[1], rom_1_data_2[3], rom_1_data_2[2], rom_1_data_2[0]);  // AND_Gate

  // Notes on the sheet:
  //   contents of rom_1 (hex, n*v repeats v):
  //   0 122 1b 2b 3b 4b ffb e7 0 0 0 2a
endmodule
